// Logisim project 16BitsAdder.circ as structural Verilog: 5 circuits, main circuit halfAdder
module halfAdder (
  input  A,
  input  B,
  output S,
  output CO
);

  xor xor_1 (S, A, B);
  and and_1 (CO, A, B);
endmodule

module fullAdder (
  input  CI,
  input  A,
  input  B,
  output S,
  output CO
);

  wire halfadder_1_co, halfadder_1_s, halfadder_2_co;

  halfAdder halfadder_1 (.A(A), .B(B), .S(halfadder_1_s), .CO(halfadder_1_co));
  halfAdder halfadder_2 (.A(CI), .B(halfadder_1_s), .S(S), .CO(halfadder_2_co));
  or or_1 (CO, halfadder_2_co, halfadder_1_co);
endmodule

module adder8Bits (
  input  C0,
  input  A0,
  input  B0,
  input  A1,
  input  B1,
  input  A2,
  input  B2,
  input  A3,
  input  B3,
  input  A4,
  input  B4,
  input  A5,
  input  B5,
  input  A6,
  input  B6,
  input  A7,
  input  B7,
  output S0,
  output S1,
  output S2,
  output S3,
  output S4,
  output S5,
  output S6,
  output S7,
  output C7
);

  wire fulladder_1_co, fulladder_2_co, fulladder_3_co, fulladder_4_co, fulladder_5_co, fulladder_6_co,
       fulladder_7_co;

  fullAdder fulladder_1 (.CI(C0), .A(A0), .B(B0), .S(S0), .CO(fulladder_1_co));
  fullAdder fulladder_2 (.CI(fulladder_1_co), .A(A1), .B(B1), .S(S1), .CO(fulladder_2_co));
  fullAdder fulladder_3 (.CI(fulladder_2_co), .A(A2), .B(B2), .S(S2), .CO(fulladder_3_co));
  fullAdder fulladder_4 (.CI(fulladder_3_co), .A(A3), .B(B3), .S(S3), .CO(fulladder_4_co));
  fullAdder fulladder_5 (.CI(fulladder_4_co), .A(A4), .B(B4), .S(S4), .CO(fulladder_5_co));
  fullAdder fulladder_6 (.CI(fulladder_5_co), .A(A5), .B(B5), .S(S5), .CO(fulladder_6_co));
  fullAdder fulladder_7 (.CI(fulladder_6_co), .A(A6), .B(B6), .S(S6), .CO(fulladder_7_co));
  fullAdder fulladder_8 (.CI(fulladder_7_co), .A(A7), .B(B7), .S(S7), .CO(C7));
endmodule

module adder16Bits (
  input  C0,
  input  A0,
  input  B0,
  input  A1,
  input  B1,
  input  A2,
  input  B2,
  input  A3,
  input  B3,
  input  A4,
  input  B4,
  input  A5,
  input  B5,
  input  A6,
  input  B6,
  input  A7,
  input  B7,
  input  A8,
  input  B8,
  input  A9,
  input  B9,
  input  A10,
  input  B10,
  input  A11,
  input  B11,
  input  A12,
  input  B12,
  input  A13,
  input  B13,
  input  A14,
  input  B14,
  input  A15,
  input  B15,
  output S0,
  output S1,
  output S2,
  output S3,
  output S4,
  output S5,
  output S6,
  output S7,
  output S8,
  output S9,
  output S10,
  output S11,
  output S12,
  output S13,
  output S14,
  output S15,
  output C16
);

  wire adder8bits_1_c7;

  adder8Bits adder8bits_1 (
    .C0(C0), .A0(A0), .B0(B0), .A1(A1), .B1(B1), .A2(A2), .B2(B2), .A3(A3), .B3(B3), .A4(A4), .B4(B4),
    .A5(A5), .B5(B5), .A6(A6), .B6(B6), .A7(A7), .B7(B7), .S0(S0), .S1(S1), .S2(S2), .S3(S3), .S4(S4),
    .S5(S5), .S6(S6), .S7(S7), .C7(adder8bits_1_c7));
  adder8Bits adder8bits_2 (
    .C0(adder8bits_1_c7), .A0(A8), .B0(B8), .A1(A9), .B1(B9), .A2(A10), .B2(B10), .A3(A11), .B3(B11),
    .A4(A12), .B4(B12), .A5(A13), .B5(B13), .A6(A14), .B6(B14), .A7(A15), .B7(B15), .S0(S8), .S1(S9),
    .S2(S10), .S3(S11), .S4(S12), .S5(S13), .S6(S14), .S7(S15), .C7(C16));
endmodule

module adderSubtractor (
  input  M,
  input  A0,
  input  B0,
  input  A1,
  input  B1,
  input  A2,
  input  B2,
  input  A3,
  input  A3_2,
  input  A4,
  input  B4,
  input  A5,
  input  B5,
  input  A6,
  input  B6,
  input  A7,
  input  B7,
  output S0,
  output S1,
  output S2,
  output S3,
  output S4,
  output S5,
  output S6,
  output S7
);

  wire fulladder_1_co, fulladder_2_co, fulladder_3_co, fulladder_4_co, fulladder_5_co, fulladder_6_co,
       fulladder_7_co, xor_1_out, xor_2_out, xor_3_out, xor_4_out, xor_5_out, xor_6_out, xor_7_out, xor_8_out;

  fullAdder fulladder_1 (.CI(M), .A(A0), .B(xor_1_out), .S(S0), .CO(fulladder_1_co));
  xor xor_1 (xor_1_out, B0, M);
  fullAdder fulladder_2 (.CI(fulladder_1_co), .A(A1), .B(xor_2_out), .S(S1), .CO(fulladder_2_co));
  xor xor_2 (xor_2_out, B1, M);
  fullAdder fulladder_3 (.CI(fulladder_2_co), .A(A2), .B(xor_3_out), .S(S2), .CO(fulladder_3_co));
  xor xor_3 (xor_3_out, B2, M);
  fullAdder fulladder_4 (.CI(fulladder_3_co), .A(A3), .B(xor_4_out), .S(S3), .CO(fulladder_4_co));
  xor xor_4 (xor_4_out, A3_2, M);
  fullAdder fulladder_5 (.CI(fulladder_4_co), .A(A4), .B(xor_5_out), .S(S4), .CO(fulladder_5_co));
  xor xor_5 (xor_5_out, B4, M);
  fullAdder fulladder_6 (.CI(fulladder_5_co), .A(A5), .B(xor_6_out), .S(S5), .CO(fulladder_6_co));
  xor xor_6 (xor_6_out, B5, M);
  fullAdder fulladder_7 (.CI(fulladder_6_co), .A(A6), .B(xor_7_out), .S(S6), .CO(fulladder_7_co));
  xor xor_7 (xor_7_out, B6, M);
  fullAdder fulladder_8 (.CI(fulladder_7_co), .A(A7), .B(xor_8_out), .S(S7));  // open: CO
  xor xor_8 (xor_8_out, B7, M);
endmodule
